# Fritzing sketch Program the ATTINY85 with Arduino (saved by Fritzing 0.8.3b)
breadboards: 1

parts:
  IC1_TINY_85 = IC, DIP package, 8 pins [chip_label=IC]
  Part1 = Arduino Nano (Rev3.0)
  C1 = Electrolytic Capacitor [capacitance=10µF voltage=10V package="100 mil [THT, electrolytic]"]
  C2_104 = Ceramic Capacitor [capacitance=0.1µF package="100 mil [THT, multilayer]"]

nets:
  N1: IC1_TINY_85.pin1, Part1.D10
  N2: IC1_TINY_85.pin4, Part1.D1/TX, Part1.GND, C1.-, C2_104.1
  N3: IC1_TINY_85.pin5, Part1.D11/MOSI
  N4: IC1_TINY_85.pin6, Part1.D12/MISO
  N5: IC1_TINY_85.pin7, Part1.D13/SCK
  N6: IC1_TINY_85.pin8, C2_104.0
  N7: Part1.RESET, C1.+

notes:
  Board: "Attiny 25/45/85(no Bootloader)"
  Chip: "ATtiny85"
  Clock Source(Only set on bootload):"8 MHz(internal)
  Timer 1 Clock: "CPU Frequency)"
  LTO(1.6.11+only):"Enabled"
  millis()/micros():"Enabled"
  Save EEPROM(only set on booyload):"EEPROM retained"
  B.O.D Level(Only Set on Bootload):"B.O.D Disabled (save Power)"
  Programmer: "Arduino as Isp"
