# Fritzing sketch WorkedCircuit (saved by Fritzing 0.8.3b)
breadboards: 1

parts:
  IC1_Attiny = IC, DIP package, 8 pins [chip_label=IC]
  R1 = Photocell (LDR) [package=THT]
  R2 = Resistor [tolerance=±5% resistance=10k package=THT]
  LED1 = LED - 5mm [color="Red (633nm)" package="5 mm [THT]"]
  R3 = Resistor [tolerance=±5% resistance=220 package=THT]
  R4 = Rotary Potentiometer (Small)
  VCC1 = Battery

nets:
  N1: IC1_Attiny.pin2, R4.wiper
  N2: IC1_Attiny.pin3, R1.pin_0, R2.Pin_1
  N3: IC1_Attiny.pin4, R2.Pin_0, LED1.cathode, R4.leg1, VCC1.-
  N4: IC1_Attiny.pin7, R3.Pin_0
  N5: IC1_Attiny.pin8, R1.pin_1, R4.leg2, VCC1.+
  N6: LED1.anode, R3.Pin_1
